# Fritzing sketch arduino_lcd_frontend (saved by Fritzing 0.7.10b)
breadboards: 1

parts:
  Nano1 = Arduino Nano v2.3
  LCD1 = LCD screen
  RE1 = ENCODER_2LED [package=encoder_led_2]  # not connected
  RE2 = Rotary Encoder [package=THT]
  R1 = Trimmer Potentiometer [maximum_resistance=10kΩ package=THT]
  R2 = Resistor [tolerance=±5% resistance=220 package=THT]
  R3 = Resistor [tolerance=±5% resistance=220 package=THT]
  LED1 = LED - 5mm [color="Red (633nm)" package="5 mm [THT]"]
  LED2 = LED - 5mm [color="Green (570nm)" package="5 mm [THT]"]
  S1 = Pushbutton [package="[THT]"]

nets:
  GND: Nano1.GND, LCD1.VSS, LCD1.R/W, LCD1.LED-, RE2.EncoderPinC, R1.leg1, R2.Pin_1, R3.Pin_1, S1.Pin_3, S1.Pin_4
  N1: Nano1.D2, RE2.EncoderPinB
  N2: Nano1.D3, RE2.EncoderPinA
  N3: Nano1.D4, S1.Pin_1, S1.Pin_2
  N4: Nano1.D5, LED1.anode
  N5: Nano1.D6, LED2.anode
  N6: Nano1.D7, LCD1.DB7
  N7: Nano1.D8, LCD1.DB6
  N8: Nano1.D9, LCD1.DB5
  N9: Nano1.D10, LCD1.DB4
  N10: Nano1.D11, LCD1.E
  N11: Nano1.D12, LCD1.RS
  N12: Nano1.D13, LCD1.LED+
  +5V: Nano1.+5V, LCD1.VDD, R1.leg2
  N13: LCD1.V0, R1.wiper
  N14: R2.Pin_0, LED1.cathode
  N15: R3.Pin_0, LED2.cathode
